# Fritzing sketch oledCursor (saved by Fritzing 0.9.3b)
breadboards: 1

parts:
  Part1 = OLED Monochrome 128x64 0.96 inch [part_number=326]
  Part2 = Arduino Uno (Rev3)
  Part3 = Thumb Joystick

nets:
  N1: Part1.MOSI_SDA, Part2.D9_PWM
  N2: Part1.SCLK_SCK, Part2.D10_PWM/SS
  N3: Part1.DC_SA0, Part2.D11_PWM/MOSI
  N4: Part1.RESET, Part2.D13/SCK
  VIN: Part1.VIN, Part2.5V, Part3.VCC
  GND: Part1.GND, Part2.GND, Part3.GND
  N5: Part2.A0, Part3.HORZ
  N6: Part2.A1, Part3.VERT
  N7: Part2.D7, Part3.SEL

custom parts:
  OLED Monochrome 128x64 0.96 inch: These displays are small, only about 1" diameter, but very readable due to the high contrast of an OLED display. This display is made of 128x64 individual white OLED pixels, each one is turned on or off by the controller chip. Because the display makes its own light, no backlight is required. This reduces the power required to run the OLED and is why the display has such high contrast; we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
